# Fritzing sketch microbit_bmp280_dht11 (saved by Fritzing 0.9.3b)
breadboards: 1

parts:
  M1 = Humidity and Temperature Sensor DHT11
  R1 = Resistor [tolerance=±5% resistance=10k package="0805 [SMD]"]
  M2 = BME280
  Mod1 = Microbit

nets:
  VCC: M1.Vcc, R1.Pin_0, M2.VIN, Mod1.3V3-bot
  N1: M1.Data, R1.Pin_1, Mod1.P0-bot
  GND: M1.GND, M2.GND, Mod1.GND-18
  N2: M2.SCL, Mod1.P19-bot
  N3: M2.SDA, Mod1.P20-bot

custom parts:
  Humidity and Temperature Sensor DHT11: Digital relative humidity & temperature sensor DHT11
  BME280: Temperature Humidity Barometric presure Sensor
  Microbit: BBC Microbit Fritzing part. July 2020 modify to match the xxx breakout board from yyyy. Remove pcb view as unused (this is a breakout board) and add all the connectors on the breakout board (not all of which I know the purpose of at the moment.)
